# Fritzing sketch Esboço_Projeto (saved by Fritzing 0.9.3b)
breadboards: 1

parts:
  U1 = NodeMCU V1.0
  HC-SR04_Sensor_1 = HC-SR04 Ultrasonic Distance Sensor
  R2 = Resistor [tolerance=±5% resistance=1k package=THT]  # not connected
  R1 = Resistor [tolerance=±5% resistance=1k package="2512 [SMD]"]
  R3 = Resistor [tolerance=±5% resistance=1k package=THT]
  R4 = Resistor [tolerance=±5% resistance=1k package=THT]
  S3 = Tilt Switch [package=THT]
  S4 = Tilt Switch [package=THT]

nets:
  GND: U1.D0, U1.D1, U1.GND, HC-SR04_Sensor_1.GND, R1.Pin_0, R3.Pin_1, R4.Pin_1
  N1: U1.D2, HC-SR04_Sensor_1.TRIG
  N2: U1.D5, R1.Pin_1
  VIN: U1.Vin, HC-SR04_Sensor_1.VCC
  N3: U1.3V3, S3.Pin_2, S4.Pin_2
  N4: R3.Pin_0, S4.Pin_1
  N5: R4.Pin_0, S3.Pin_1

custom parts:
  NodeMCU V1.0: ESP8266 based NodeMCU
